// Logisim project DAAC PR2_4_mod.circ as structural Verilog: 1 circuit, main circuit main
module main (
  input  Paridad,
  input  in_2,
  input  in_3,
  input  in_4,
  input  Dato,
  input  in_6,
  input  in_7,
  input  in_8,
  input  in_9,
  input  Inicio,
  input  Receptor,
  input  in_12,
  input  Receptor_2,
  input  in_14,
  input  in_15,
  input  Dato_2,
  input  in_17,
  input  in_18,
  input  Desplazamiento,
  input  Desplazamiento_2,
  input  Salida,
  input  Salida_2,
  output [7:0] out_23,
  output [7:0] out_24
);

  wire and_1_out, and_2_out, and_3_out, clock_1_out, controlled_buffer_1_out, controlled_buffer_2_out,
       not_1_out, not_2_out, shift_register_1_out, shift_register_1_q0, shift_register_1_q1,
       shift_register_2_out, undriven;
  wire [3:0] counter_1_q;
  wire [7:0] shift_register_1_q11, shift_register_2_q7;

  Shift_Register #(.length(13)) shift_register_1 (
    .shift(Desplazamiento_2), .in(controlled_buffer_2_out), .clk(and_2_out), .out(shift_register_1_out),
    .load(Inicio), .d0(Receptor), .q0(shift_register_1_q0), .d1(in_12), .q1(shift_register_1_q1), .d2(1'b1),
    .d3(1'b1), .d4(in_2), .q4(shift_register_1_q11[7]), .d5(in_3), .q5(shift_register_1_q11[6]), .d6(in_4),
    .q6(shift_register_1_q11[5]), .d7(Dato), .q7(shift_register_1_q11[4]), .d8(in_6),
    .q8(shift_register_1_q11[3]), .d9(in_7), .q9(shift_register_1_q11[2]), .d10(in_8),
    .q10(shift_register_1_q11[1]), .d11(in_9), .q11(shift_register_1_q11[0]), .d12(undriven));  // open: clr, q2, q3, q12
  and and_1 (and_1_out, shift_register_1_q1, shift_register_1_q0, Salida, counter_1_q[3]);
  assign controlled_buffer_1_out = Salida ? shift_register_1_out : 1'bz;  // Controlled_Buffer controlled_buffer_1
  Hex_Digit_Display hex_digit_display_1 (.value(out_23[7:4]));  // open: dp
  Register register_1 (.D(shift_register_1_q11), .Q(out_23), .clk(and_1_out));  // open: en, clr
  Hex_Digit_Display hex_digit_display_2 (.value(out_23[3:0]));  // open: dp
  Counter #(.width(4), .max('hf)) counter_1 (
    .Q(counter_1_q), .clk(and_2_out), .clr(Inicio));  // open: load, D, count, carry
  Clock clock_1 (.out(clock_1_out));
  not not_1 (not_1_out, counter_1_q[3]);
  and and_2 (and_2_out, clock_1_out, not_1_out);
  not not_2 (not_2_out, shift_register_2_q7[7]);
  Shift_Register shift_register_2 (
    .shift(Desplazamiento), .in(controlled_buffer_1_out), .clk(and_2_out), .out(shift_register_2_out),
    .load(Inicio), .d0(Receptor_2), .q0(shift_register_2_q7[7]), .d1(in_14), .q1(shift_register_2_q7[6]),
    .d2(1'b0), .q2(shift_register_2_q7[5]), .d3(1'b1), .q3(shift_register_2_q7[4]), .d4(in_15),
    .q4(shift_register_2_q7[3]), .d5(Dato_2), .q5(shift_register_2_q7[2]), .d6(in_17),
    .q6(shift_register_2_q7[1]), .d7(in_18), .q7(shift_register_2_q7[0]));  // open: clr
  and and_3 (and_3_out, shift_register_2_q7[6], not_2_out, Salida_2, counter_1_q[3]);
  assign controlled_buffer_2_out = Salida_2 ? shift_register_2_out : 1'bz;  // Controlled_Buffer controlled_buffer_2
  Hex_Digit_Display hex_digit_display_3 (.value(out_24[7:4]));  // open: dp
  Register register_2 (.D(shift_register_2_q7), .Q(out_24), .clk(and_3_out));  // open: en, clr
  Hex_Digit_Display hex_digit_display_4 (.value(out_24[3:0]));  // open: dp

  // Notes on the sheet:
  //   Fuente
  //   Nº de registro= 11
  //   Fuente
  //   Nº de registro = 01
endmodule
